// Logisim project LC-2200-16.circ as structural Verilog: 7 circuits, main circuit main
// DataPath
module main (
  input  in_1,
  input  in_2,
  input  in_3,
  input  in_4,
  input  in_5,
  input  in_6,
  input  in_7,
  input  in_8,
  input  in_9,
  input  in_10,
  input  in_11,
  input  in_12,
  input  in_13,
  input  in_14,
  input  in_15,
  input  in_16,
  input  in_17,
  input  in_18,
  output [2:0] Op_Code,
  output [15:0] Value_On_Bus,
  output [3:0] regno,
  output [15:0] RegOut,
  output Z
);

  wire Clk, nor_1_out;
  wire [12:0] IR;
  wire [15:0] A_q, ALU_o, B_q, bit_extender_1_out, MAR_q, PC_q, ram_1_data;

  Clock clock_1 (.out(Clk));
  assign Value_On_Bus = in_4 ? PC_q : 16'bz;  // Controlled_Buffer controlled_buffer_1
  Register #(.width(16)) PC (.en(in_13), .Q(PC_q), .clk(Clk), .clr(in_3));  // open: D
  Register #(.width(16)) B (.D(Value_On_Bus), .en(in_15), .Q(B_q), .clk(Clk), .clr(in_3));
  _16_bit_ALU ALU (.A(A_q), .B(B_q), .func({in_7, in_5}), .O(ALU_o));
  assign Value_On_Bus = in_6 ? ALU_o : 16'bz;  // Controlled_Buffer controlled_buffer_2
  nor nor_1 (nor_1_out, Value_On_Bus[15], Value_On_Bus[14], Value_On_Bus[13], Value_On_Bus[12], Value_On_Bus[11], Value_On_Bus[10], Value_On_Bus[9], Value_On_Bus[8], Value_On_Bus[7], Value_On_Bus[6], Value_On_Bus[5], Value_On_Bus[4], Value_On_Bus[3], Value_On_Bus[2], Value_On_Bus[1], Value_On_Bus[0]);
  Register #(.width(16)) A (.D(Value_On_Bus), .en(in_14), .Q(A_q), .clk(Clk), .clr(in_3));
  _16_Register_File Registers (.Din(Value_On_Bus), .regno(regno), .wrREG(in_2), .Dout(RegOut));
  assign Value_On_Bus = in_8 ? RegOut : 16'bz;  // Controlled_Buffer controlled_buffer_3
  Register #(.width(1)) register_1 (.D(nor_1_out), .en(in_18), .Q(Z), .clk(Clk), .clr(in_3));
  Register #(.width(16)) MAR (.D(Value_On_Bus), .en(in_16), .Q(MAR_q), .clk(Clk), .clr(in_3));
  RAM #(.addrWidth(16), .dataWidth(16), .bus("separate")) ram_1 (
    .addr(MAR_q), .din(Value_On_Bus), .data(ram_1_data), .str(in_1), .clk(Clk), .ld(1'b1), .clr(in_3));  // open: sel
  assign Value_On_Bus = in_10 ? ram_1_data : 16'bz;  // Controlled_Buffer controlled_buffer_4
  Register #(.width(16)) u_IR (.D(Value_On_Bus), .en(in_17), .Q({Op_Code, IR}), .clk(Clk), .clr(in_3));
  assign bit_extender_1_out = {{11{IR[4]}}, IR[4:0]};  // Bit_Extender bit_extender_1
  assign Value_On_Bus = in_12 ? bit_extender_1_out : 16'bz;  // Controlled_Buffer controlled_buffer_5
  Multiplexer #(.select(2), .width(4), .disabled(0), .enable("false")) multiplexer_1 (
    .in0(IR[12:9]), .in1(IR[8:5]), .in2({IR[0], IR[1], IR[2], IR[3]}), .out(regno), .sel({in_11, in_9}));  // open: in3

  // Other names for the same wires on the sheet: Clr = in_3; DrALU = in_6; DrMEM = in_10; DrOFF = in_12; DrPC = in_4;
  //   DrREG = in_8; ALULo = in_5; func[1:0] = {in_7, in_5}; ALUHi = in_7; LdA = in_14; LdB = in_15; LdIR = in_17;
  //   LdMAR = in_16; LdPC = in_13; LdZ = in_18; Offset[4:0] = IR[4:0]; RZ[3:0] = {IR[0], IR[1], IR[2], IR[3]};
  //   IR[15:13] = Op_Code; Reg_Sel[1:0] = {in_11, in_9}; RegSelLo = in_9; RegSelHi = in_11; RX[3:0] = IR[12:9];
  //   RY[3:0] = IR[8:5]; wrMEM = in_1; wrREG = in_2
endmodule

module _1_bit_Adder (
  input  A,
  input  B,
  input  CIn,
  output O,
  output COut
);

  wire and_1_out, and_2_out, and_3_out, or_1_out, xor_1_out;

  xor xor_1 (xor_1_out, A, B);
  and and_1 (and_1_out, A, B);
  and and_2 (and_2_out, B, CIn);
  and and_3 (and_3_out, A, CIn);
  or or_1 (or_1_out, and_1_out, and_2_out);
  xor xor_2 (O, xor_1_out, CIn);
  or or_2 (COut, or_1_out, and_3_out);
endmodule

module _4_bit_Adder (
  input  [3:0] A,
  input  [3:0] B,
  input  Cin,
  output [3:0] O,
  output Cout
);

  wire COut0, COut1, COut2;

  _1_bit_Adder u_1_bit_adder_1 (.A(A[0]), .B(B[0]), .CIn(Cin), .O(O[0]), .COut(COut0));
  _1_bit_Adder u_1_bit_adder_2 (.A(A[1]), .B(B[1]), .CIn(COut0), .O(O[1]), .COut(COut1));
  _1_bit_Adder u_1_bit_adder_3 (.A(A[2]), .B(B[2]), .CIn(COut1), .O(O[2]), .COut(COut2));
  _1_bit_Adder u_1_bit_adder_4 (.A(A[3]), .B(B[3]), .CIn(COut2), .O(O[3]), .COut(Cout));

  // Other names for the same wires on the sheet: Bit0 = O[0]; Bit1 = O[1]; Bit2 = O[2]; Bit3 = O[3]
endmodule

module _16_bit_Adder (
  input  [15:0] A,
  input  [15:0] B,
  input  Cin,
  output [15:0] O,
  output Cout
);

  wire COut0, COut1, COut2;

  _4_bit_Adder u_4_bit_adder_1 (.A(A[3:0]), .B(B[3:0]), .Cin(Cin), .O(O[3:0]), .Cout(COut0));
  _4_bit_Adder u_4_bit_adder_2 (.A(A[7:4]), .B(B[7:4]), .Cin(COut0), .O(O[7:4]), .Cout(COut1));
  _4_bit_Adder u_4_bit_adder_3 (.A(A[11:8]), .B(B[11:8]), .Cin(COut1), .O(O[11:8]), .Cout(COut2));
  _4_bit_Adder u_4_bit_adder_4 (.A(A[15:12]), .B(B[15:12]), .Cin(COut2), .O(O[15:12]), .Cout(Cout));

  // Other names for the same wires on the sheet: A0[3:0] = A[3:0]; A1[3:0] = A[7:4]; A2[3:0] = A[11:8];
  //   A3[3:0] = A[15:12]; B0[3:0] = B[3:0]; B1[3:0] = B[7:4]; B2[3:0] = B[11:8]; B3[3:0] = B[15:12];
  //   Bit0[3:0] = O[3:0]; Bit1[3:0] = O[7:4]; Bit2[3:0] = O[11:8]; Bit3[3:0] = O[15:12]
endmodule

module _16_bit_ALU (
  input  [15:0] A,
  input  [15:0] B,
  input  [1:0] func,
  output [15:0] O
);

  wire [15:0] Addition, Increment, NAND, not_1_out, Subtraction;

  assign not_1_out = ~B;  // NOT_Gate not_1, 16 bits wide
  _16_bit_Adder u_16_bit_adder_1 (.A(A), .B(B), .Cin(1'b0), .O(Addition));  // open: Cout
  assign Subtraction = A & not_1_out;  // AND_Gate and_1, 16 bits wide
  _16_bit_Adder u_16_bit_adder_2 (.A(A), .B(16'h1), .Cin(1'b0), .O(Increment));  // open: Cout
  assign NAND = ~(A & B);  // NAND_Gate nand_1, 16 bits wide
  Multiplexer #(.select(2), .width(16), .disabled(0), .enable("false")) multiplexer_1 (
    .in0(Addition), .in1(NAND), .in2(Subtraction), .in3(Increment), .out(O), .sel(func));
endmodule

module _16_Register_File (
  input  [15:0] Din,
  input  [3:0] regno,
  input  wrREG,
  output [15:0] Dout
);

  wire and_1_out, and_2_out, and_3_out, and_4_out, and_5_out, and_6_out, and_7_out, and_8_out, and_9_out,
       and_10_out, and_11_out, and_12_out, and_13_out, and_14_out, and_15_out, and_16_out, not_1_out,
       not_2_out, not_3_out, not_4_out, not_5_out, not_6_out, not_7_out, not_8_out, not_9_out, not_10_out,
       not_11_out, not_12_out, not_13_out, not_14_out, not_15_out, not_16_out, not_17_out, not_18_out,
       not_19_out, not_20_out, not_21_out, not_22_out, not_23_out, not_24_out, not_25_out, not_26_out,
       not_27_out, not_28_out, not_29_out, not_30_out, not_31_out, not_32_out;
  wire [15:0] register_1_q, register_2_q, register_3_q, register_4_q, register_5_q, register_6_q,
       register_7_q, register_8_q, register_9_q, register_10_q, register_11_q, register_12_q, register_13_q,
       register_14_q, register_15_q, register_16_q;

  not not_1 (not_1_out, regno[0]);
  not not_2 (not_2_out, regno[1]);
  not not_3 (not_3_out, regno[2]);
  not not_4 (not_4_out, regno[3]);
  not not_5 (not_5_out, regno[1]);
  not not_6 (not_6_out, regno[2]);
  not not_7 (not_7_out, regno[3]);
  not not_8 (not_8_out, regno[0]);
  not not_9 (not_9_out, regno[2]);
  not not_10 (not_10_out, regno[3]);
  not not_11 (not_11_out, regno[2]);
  not not_12 (not_12_out, regno[3]);
  not not_13 (not_13_out, regno[0]);
  not not_14 (not_14_out, regno[1]);
  not not_15 (not_15_out, regno[3]);
  not not_16 (not_16_out, regno[1]);
  not not_17 (not_17_out, regno[3]);
  not not_18 (not_18_out, regno[0]);
  not not_19 (not_19_out, regno[3]);
  not not_20 (not_20_out, regno[3]);
  not not_21 (not_21_out, regno[0]);
  not not_22 (not_22_out, regno[1]);
  not not_23 (not_23_out, regno[2]);
  not not_24 (not_24_out, regno[1]);
  not not_25 (not_25_out, regno[2]);
  not not_26 (not_26_out, regno[0]);
  not not_27 (not_27_out, regno[2]);
  not not_28 (not_28_out, regno[2]);
  not not_29 (not_29_out, regno[0]);
  not not_30 (not_30_out, regno[1]);
  not not_31 (not_31_out, regno[1]);
  not not_32 (not_32_out, regno[0]);
  and and_1 (and_1_out, not_1_out, not_2_out, not_3_out, not_4_out, wrREG);
  and and_2 (and_2_out, regno[0], not_5_out, not_6_out, not_7_out, wrREG);
  and and_3 (and_3_out, not_8_out, regno[1], not_9_out, not_10_out, wrREG);
  and and_4 (and_4_out, regno[0], regno[1], not_11_out, not_12_out, wrREG);
  and and_5 (and_5_out, not_13_out, not_14_out, regno[2], not_15_out, wrREG);
  and and_6 (and_6_out, regno[0], not_16_out, regno[2], not_17_out, wrREG);
  and and_7 (and_7_out, not_18_out, regno[1], regno[2], not_19_out, wrREG);
  and and_8 (and_8_out, regno[0], regno[1], regno[2], not_20_out, wrREG);
  and and_9 (and_9_out, not_21_out, not_22_out, not_23_out, regno[3], wrREG);
  and and_10 (and_10_out, regno[0], not_24_out, not_25_out, regno[3], wrREG);
  and and_11 (and_11_out, not_26_out, regno[1], not_27_out, regno[3], wrREG);
  and and_12 (and_12_out, regno[0], regno[1], not_28_out, regno[3], wrREG);
  and and_13 (and_13_out, not_29_out, not_30_out, regno[2], regno[3], wrREG);
  and and_14 (and_14_out, regno[0], not_31_out, regno[2], regno[3], wrREG);
  and and_15 (and_15_out, not_32_out, regno[1], regno[2], regno[3], wrREG);
  and and_16 (and_16_out, regno[0], regno[1], regno[2], regno[3], wrREG);
  Register #(.width(16)) register_1 (.D(Din), .Q(register_1_q), .clk(and_1_out));  // open: en, clr
  Register #(.width(16)) register_2 (.D(Din), .Q(register_2_q), .clk(and_2_out));  // open: en, clr
  Register #(.width(16)) register_3 (.D(Din), .Q(register_3_q), .clk(and_3_out));  // open: en, clr
  Register #(.width(16)) register_4 (.D(Din), .Q(register_4_q), .clk(and_4_out));  // open: en, clr
  Register #(.width(16)) register_5 (.D(Din), .Q(register_5_q), .clk(and_5_out));  // open: en, clr
  Register #(.width(16)) register_6 (.D(Din), .Q(register_6_q), .clk(and_6_out));  // open: en, clr
  Register #(.width(16)) register_7 (.D(Din), .Q(register_7_q), .clk(and_7_out));  // open: en, clr
  Register #(.width(16)) register_8 (.D(Din), .Q(register_8_q), .clk(and_8_out));  // open: en, clr
  Register #(.width(16)) register_9 (.D(Din), .Q(register_9_q), .clk(and_9_out));  // open: en, clr
  Register #(.width(16)) register_10 (.D(Din), .Q(register_10_q), .clk(and_10_out));  // open: en, clr
  Register #(.width(16)) register_11 (.D(Din), .Q(register_11_q), .clk(and_11_out));  // open: en, clr
  Register #(.width(16)) register_12 (.D(Din), .Q(register_12_q), .clk(and_12_out));  // open: en, clr
  Register #(.width(16)) register_13 (.D(Din), .Q(register_13_q), .clk(and_13_out));  // open: en, clr
  Register #(.width(16)) register_14 (.D(Din), .Q(register_14_q), .clk(and_14_out));  // open: en, clr
  Register #(.width(16)) register_15 (.D(Din), .Q(register_15_q), .clk(and_15_out));  // open: en, clr
  Register #(.width(16)) register_16 (.D(Din), .Q(register_16_q), .clk(and_16_out));  // open: en, clr
  Multiplexer #(.select(4), .width(16), .enable("false")) multiplexer_1 (
    .in0(register_1_q), .in1(register_2_q), .in2(register_3_q), .in3(register_4_q), .in4(register_5_q),
    .in5(register_6_q), .in6(register_7_q), .in7(register_8_q), .in8(register_9_q), .in9(register_10_q),
    .in10(register_11_q), .in11(register_12_q), .in12(register_13_q), .in13(register_14_q),
    .in14(register_15_q), .in15(register_16_q), .out(Dout), .sel(regno));
endmodule

module Microcontroller (
  input  CLR,
  output [2:0] Op_Code
);

  wire [0:0] main_1_z;
  wire [5:0] multiplexer_1_out, Next_State, register_1_q, rom_2_data, rom_3_data;
  wire [24:6] rom_1_data;

  ROM #(.addrWidth(6), .dataWidth(25)) rom_1 (.addr(register_1_q), .data({rom_1_data, Next_State}));  // open: sel
  Register #(.width(6)) register_1 (.D(multiplexer_1_out), .Q(register_1_q));  // open: en, clk, clr
  main main_1 (
    .in_1(rom_1_data[18]), .in_2(rom_1_data[17]), .Op_Code(Op_Code), .in_4(rom_1_data[9]),
    .in_6(rom_1_data[8]), .in_8(rom_1_data[6]), .in_10(rom_1_data[7]), .in_12(rom_1_data[10]),
    .Z(main_1_z[0]), .in_13(rom_1_data[11]), .in_14(rom_1_data[14]), .in_15(rom_1_data[15]),
    .in_16(rom_1_data[13]), .in_17(rom_1_data[12]), .in_18(rom_1_data[16]), .in_3(CLR),
    .in_5(rom_1_data[22]), .in_7(rom_1_data[21]), .in_9(rom_1_data[19]), .in_11(rom_1_data[20]));  // open: RegOut, Value_On_Bus, regno
  Multiplexer #(.select(2), .width(6), .disabled(0), .enable("false")) multiplexer_1 (
    .in0(Next_State), .in1(rom_3_data), .in2(rom_2_data), .out(multiplexer_1_out), .sel(rom_1_data[24:23]));  // open: in3
  ROM #(.addrWidth(2), .dataWidth(6)) rom_2 (.addr({1'b0, main_1_z[0]}), .data(rom_2_data));  // open: sel
  ROM #(.addrWidth(3), .dataWidth(6)) rom_3 (.addr(Op_Code), .data(rom_3_data));  // open: sel
endmodule
